# Fritzing sketch SensorLed (saved by Fritzing 0.8.5b)
breadboards: 1

parts:
  Componente2 = Arduino Uno (Rev3)
  U2 = GAS_SENSOR [package=mq-3]
  LED1 = LED - 5mm [color="Red (633nm)" package="5 mm [THT]"]
  R1 = Resistor [tolerance=±5% resistance=220 package=THT]

nets:
  N1: Componente2.A1, U2.A1
  N2: Componente2.D9_PWM, LED1.anode
  N3: Componente2.GND, U2.H1, R1.Pin_1
  N4: Componente2.5V, U2.H2
  N5: LED1.cathode, R1.Pin_0
