# Fritzing sketch SensorServo_Sketch (saved by Fritzing 0.8.5b)

parts:
  Componente1 = Arduino Uno (Rev3)
  J1 = Basic Servo
  U1 = GAS_SENSOR [package=mq-3]

nets:
  N1: Componente1.A1, U1.A1
  N2: Componente1.D9_PWM, J1.pulse
  GND: Componente1.GND, J1.gnd, U1.H1
  5V: Componente1.5V, J1.vcc, U1.H2
