# Fritzing sketch gasvisual (saved by Fritzing 0.8.5b)

parts:
  Componente2 = Arduino Uno (Rev3)
  U2 = GAS_SENSOR [package=mq-3]

nets:
  N1: Componente2.A1, U2.A1
  N2: Componente2.5V, U2.H2
  N3: Componente2.GND, U2.H1
